# Fritzing sketch Schematic (saved by Fritzing 0.9.3b)
breadboards: 1

parts:
  Part1 = Arduino Mega 2560 (Rev3)
  R1 = Rotary Potentiometer (Small) [maximum_resistance=100kΩ package=THT]
  R2 = Rotary Potentiometer (Small) [maximum_resistance=100kΩ package=THT]
  SP1 = SPEAKER [package=pcb_mount_speaker]
  Q1 = NPN-Transistor [package="TO92 [THT]"]
  Part2 = MicroSD Card Module
  R3 = Resistor [tolerance=±5% resistance=4.7k package=THT]

nets:
  N1: Part1.A0, R2.wiper
  N2: Part1.A1, R1.wiper
  5V: Part1.5V, R1.leg1, R2.leg1, SP1.-, Part2.VCC
  GND: Part1.GND, R1.leg2, R2.leg2, Q1.E, Part2.GND
  N3: Part1.D2_PWM, R3.Pin_0
  N4: Part1.D50, Part2.MISO
  N5: Part1.D51, Part2.MOSI
  N6: Part1.D52, Part2.SCK
  N7: Part1.D53, Part2.CS
  N8: SP1.+, Q1.C
  N9: Q1.B, R3.Pin_1

notes:
  4.7K

custom parts:
  MicroSD Card Module: A common microSD card module.
